# Fritzing sketch RFID-RC522 (saved by Fritzing 0.9.0b)
breadboards: 1

parts:
  RFID-RC522 = RFID-RC522
  R1 = Resistor [tolerance=±5% resistance=220k package=THT]
  R3 = Resistor [tolerance=±5% resistance=220k package=THT]
  Bauteil1 = Arduino Uno (Rev3) - ICSP
  LED1 = RGB LED (com. anode, rbg) [package="5 mm [THT]"]
  R4 = Resistor [tolerance=±5% resistance=220k package=THT]

nets:
  N1: RFID-RC522.SDA, Bauteil1.D10_PWM/SS
  N2: RFID-RC522.SCK, Bauteil1.ICSP_SCK, Bauteil1.D13/SCK
  N3: RFID-RC522.MOSI, Bauteil1.ICSP_MOSI, Bauteil1.D11_PWM/MOSI
  N4: RFID-RC522.MISO, Bauteil1.ICSP_MISO, Bauteil1.D12/MISO
  GND: RFID-RC522.GND, Bauteil1.GND
  N5: RFID-RC522.RST, Bauteil1.D9_PWM
  N6: RFID-RC522.3_3V, Bauteil1.3V3
  N7: R1.Pin_0, R1.Pin_1, Bauteil1.D3_PWM, LED1.red_cathode
  N8: R3.Pin_0, R3.Pin_1, Bauteil1.D6_PWM, LED1.green_cathode
  N9: Bauteil1.D5_PWM, LED1.blue_cathode, R4.Pin_0, R4.Pin_1
  N10: Bauteil1.5V, LED1.common_anode

custom parts:
  RFID-RC522: The simple China made RFID reader
